// Logisim project Aula-Plex.circ as structural Verilog: 4 circuits, main circuit main
module main (
  input  I0,
  input  I1,
  input  A,
  input  in_4,
  input  in_5,
  input  in_6,
  input  in_7,
  input  in_8,
  input  in_9,
  input  in_10,
  input  in_11,
  input  in_12,
  input  in_13,
  input  in_14,
  input  in_15,
  input  in_16,
  input  in_17,
  input  in_18,
  input  in_19,
  input  in_20,
  input  in_21,
  input  in_22,
  input  in_23,
  output Z,
  output out_25,
  output out_26,
  output out_27
);

  wire and_1_out, and_2_out, not_1_out;

  not not_1 (not_1_out, A);
  Multiplexer #(.select(3)) multiplexer_1 (
    .in0(in_4), .in1(in_6), .in2(in_8), .in3(in_10), .in4(in_12), .in5(in_13), .in6(in_15), .in7(in_18),
    .out(out_25), .sel({in_19, in_20, in_21}), .en(in_14));
  and and_1 (and_1_out, I0, not_1_out);
  and and_2 (and_2_out, I1, A);
  or or_1 (Z, and_1_out, and_2_out);
  Multiplexer #(.select(2), .enable("false")) multiplexer_2 (
    .in0(in_5), .in1(in_7), .in2(in_9), .in3(in_11), .out(out_26), .sel({in_16, in_17}));
  Multiplexer #(.select(2), .enable("false")) multiplexer_3 (
    .in0(1'b1), .in1(1'b0), .in2(1'b1), .in3(1'b0), .out(out_27), .sel({in_22, in_23}));
endmodule

module MUX4 (
  input  I0,
  input  I1,
  input  I2,
  input  I3,
  input  A,
  input  B,
  output Z
);

  wire and_1_out, and_2_out, and_3_out, and_4_out, not_1_out, not_2_out;

  not not_1 (not_1_out, A);
  not not_2 (not_2_out, B);
  and and_1 (and_1_out, I0, not_1_out, not_2_out);
  and and_2 (and_2_out, I1, not_1_out, B);
  and and_3 (and_3_out, I2, A, not_2_out);
  and and_4 (and_4_out, I3, B, A);
  or or_1 (Z, and_1_out, and_2_out, and_3_out, and_4_out);
endmodule

module _3 (
  input  A,
  input  in_2,
  input  in_3,
  output out_4
);

  Multiplexer #(.select(3), .enable("false")) multiplexer_1 (
    .in0(1'b0), .in1(1'b1), .in2(1'b0), .in3(1'b1), .in4(1'b0), .in5(1'b1), .in6(1'b1), .in7(1'b0),
    .out(out_4), .sel({A, in_2, in_3}));
endmodule

module _4 (
  input  [1:0] i,
  input  A,
  input  B,
  input  C,
  output [1:0] o1,
  output [1:0] o2,
  output [1:0] o3,
  output [1:0] o4,
  output [1:0] o5,
  output [1:0] o6,
  output [1:0] o7,
  output [1:0] o8
);

  Demultiplexer #(.select(3), .width(2), .enable("false")) demultiplexer_1 (
    .out0(o1), .out1(o2), .out2(o3), .out3(o4), .out4(o5), .out5(o6), .out6(o7), .out7(o8), .in(i),
    .sel({A, B, C}));
endmodule
