// Logisim project Cod-Dec-BCD.circ as structural Verilog: 1 circuit, main circuit main
module main (
  input  in_1,
  input  in_2,
  input  in_3,
  input  in_4,
  input  in_5,
  input  in_6,
  input  in_7,
  input  in_8,
  input  in_9,
  input  in_10
);

  wire bcd_1_s0, bcd_1_s1, bcd_1_s2, bcd_1_s3, dec_bcd_1_a, dec_bcd_1_b, dec_bcd_1_c, dec_bcd_1_d,
       dec_bcd_1_e, dec_bcd_1_f, dec_bcd_1_g;

  BCD bcd_1 (
    .e0(in_1), .s0(bcd_1_s0), .e1(in_2), .s1(bcd_1_s1), .e2(in_3), .e3(in_4), .s2(bcd_1_s2), .e4(in_5),
    .s3(bcd_1_s3), .e5(in_6), .e6(in_7), .e7(in_8), .e8(in_9), .e9(in_10));
  Dec_BCD dec_bcd_1 (
    .e3(bcd_1_s0), .e2(bcd_1_s1), .e1(bcd_1_s2), .e0(bcd_1_s3), .a(dec_bcd_1_a), .b(dec_bcd_1_b),
    .c(dec_bcd_1_c), .d(dec_bcd_1_d), .e(dec_bcd_1_e), .f(dec_bcd_1_f), .g(dec_bcd_1_g));
  _7_Segment_Display u_7_segment_display_1 (
    .g(dec_bcd_1_g), .f(dec_bcd_1_f), .a(dec_bcd_1_a), .b(dec_bcd_1_b), .e(dec_bcd_1_e), .d(dec_bcd_1_d),
    .c(dec_bcd_1_c));  // open: dp
endmodule
