// Logisim project Dec-BCD-7seg.circ as structural Verilog: 1 circuit, main circuit main
module main (
  input  in_1,
  input  in_2,
  input  in_3,
  input  in_4
);

  wire dec_bcd_1_a, dec_bcd_1_b, dec_bcd_1_c, dec_bcd_1_d, dec_bcd_1_e, dec_bcd_1_f, dec_bcd_1_g;

  Dec_BCD dec_bcd_1 (
    .e3(in_1), .e2(in_2), .e1(in_3), .e0(in_4), .a(dec_bcd_1_a), .b(dec_bcd_1_b), .c(dec_bcd_1_c),
    .d(dec_bcd_1_d), .e(dec_bcd_1_e), .f(dec_bcd_1_f), .g(dec_bcd_1_g));
  _7_Segment_Display u_7_segment_display_1 (
    .g(dec_bcd_1_g), .f(dec_bcd_1_f), .a(dec_bcd_1_a), .b(dec_bcd_1_b), .e(dec_bcd_1_e), .d(dec_bcd_1_d),
    .c(dec_bcd_1_c));  // open: dp
endmodule
