// Logisim project aula2.circ as structural Verilog: 1 circuit, main circuit main
module main (
  input  A,
  input  B,
  input  C,
  input  A_2,
  input  B_2,
  input  C_2,
  output out_7,
  output out_8
);

  wire and_1_out, and_2_out, and_3_out, and_4_out, and_5_out, and_6_out, and_7_out, and_8_out, not_1_out,
       not_2_out, not_3_out, not_4_out, not_5_out, not_6_out, not_7_out, not_8_out, not_9_out, not_10_out;

  not not_1 (not_1_out, A);
  not not_2 (not_2_out, B);
  not not_3 (not_3_out, A);
  not not_4 (not_4_out, C);
  and and_1 (and_1_out, not_1_out, not_2_out, C);
  and and_2 (and_2_out, not_3_out, B, C);
  and and_3 (and_3_out, A, B, not_4_out);
  or or_1 (out_7, and_1_out, and_2_out, and_3_out);
  not not_5 (not_5_out, A_2);
  not not_6 (not_6_out, B_2);
  and and_4 (and_4_out, not_5_out, not_6_out, not_7_out);
  not not_7 (not_7_out, C_2);
  not not_8 (not_8_out, A_2);
  and and_5 (and_5_out, not_8_out, B_2, C_2);
  not not_9 (not_9_out, B_2);
  and and_6 (and_6_out, A_2, not_9_out, C_2);
  and and_7 (and_7_out, A_2, B_2, not_10_out);
  not not_10 (not_10_out, C_2);
  and and_8 (and_8_out, A_2, B_2, C_2);
  or or_2 (out_8, and_4_out, and_5_out, and_6_out, and_7_out, and_8_out);

  // Notes on the sheet:
  //   (-A*-B*C) + (-A*B*C) + (A*B*-C)
  //   (-A*-B*-)C + (-A*B*C) + (A*-B*C) + (A*B*-C) + (A*B*C)
endmodule
