// Logisim project basico.circ as structural Verilog: 1 circuit, main circuit main
module main (
  input  in_1,
  input  in_2,
  input  in_3,
  input  in_4,
  input  in_5,
  input  in_6,
  input  in_7,
  input  in_8,
  input  in_9,
  input  \Exercício_1 ,
  input  in_11,
  input  \Exercício_2 ,
  input  in_13,
  input  in_14,
  input  in_15,
  output out_16,
  output out_17,
  output out_18,
  output out_19,
  output out_20,
  output out_21,
  output out_22,
  output out_23,
  output out_24,
  output out_25,
  output out_26,
  output out_27,
  output out_28,
  output out_29
);

  wire and_2_out, and_3_out, and_4_out, and_5_out, and_6_out, not_5_out, not_6_out, not_7_out, not_8_out,
       or_2_out, xor_2_out;

  not not_1 (out_16, in_1);
  xor xor_1 (out_17, in_2, in_2);
  xor xor_2 (xor_2_out, in_2, in_2);
  xnor xnor_1 (out_20, in_2, in_2);
  and and_1 (out_22, in_7, in_7);
  and and_2 (and_2_out, in_7, in_7);
  nand nand_1 (out_25, in_7, in_7);
  or or_1 (out_27, in_13, in_13);
  or or_2 (or_2_out, in_13, in_13);
  nor nor_1 (out_29, in_13, in_13);
  not not_2 (out_19, xor_2_out);
  not not_3 (out_23, and_2_out);
  not not_4 (out_28, or_2_out);
  not not_5 (not_5_out, in_5);
  not not_6 (not_6_out, in_3);
  not not_7 (not_7_out, in_9);
  not not_8 (not_8_out, in_6);
  and and_3 (and_3_out, in_3, not_5_out);
  and and_4 (and_4_out, not_6_out, in_5);
  and and_5 (and_5_out, in_6, not_7_out);
  and and_6 (and_6_out, not_8_out, in_9);
  or or_3 (out_24, \Exercício_1 , in_11);
  xor xor_3 (out_26, \Exercício_2 , in_14);
  or or_4 (out_18, and_3_out, and_4_out);
  nor nor_2 (out_21, and_5_out, and_6_out);

  assign in_4 = in_2;
  assign in_8 = in_7;
  assign in_15 = in_13;

  // Notes on the sheet:
  //   Teste de XOR e XNOR
  //   Teste de AND e NAND
  //   Teste de OR e NOR
  //   XOR a partir de AND e OR
  //   XNOR a partir de AND e NOR
endmodule
