// Logisim project BCD.circ as structural Verilog: 1 circuit, main circuit BCD
module BCD (
  input  e0,
  input  e1,
  input  e2,
  input  e3,
  input  e4,
  input  e5,
  input  e6,
  input  e7,
  input  e8,
  input  e9,
  output s0,
  output s1,
  output s2,
  output s3
);

  or or_1 (s0, e1, e3, e5, e7, e9);
  or or_2 (s1, e2, e3, e6, e7);
  or or_3 (s2, e4, e5, e6, e7);
  or or_4 (s3, e8, e9);
endmodule
