// Logisim project Dec-2x4.circ as structural Verilog: 1 circuit, main circuit Decod-2x4
module Decod_2x4 (
  input  e1,
  input  e0,
  output s3,
  output s2,
  output s1,
  output s0
);

  wire not_1_out, not_2_out, not_3_out, not_4_out;

  and and_1 (s3, e1, e0);
  not not_1 (not_1_out, e0);
  not not_2 (not_2_out, e1);
  not not_3 (not_3_out, e1);
  not not_4 (not_4_out, e0);
  and and_2 (s2, e1, not_1_out);
  and and_3 (s1, not_2_out, e0);
  and and_4 (s0, not_3_out, not_4_out);
endmodule
