// Logisim project cod-4x2.circ as structural Verilog: 1 circuit, main circuit Cod 4x2
module Cod_4x2 (
  input  e3,
  input  e2,
  input  e1,
  input  e0,
  output s1,
  output s0
);

  or or_1 (s1, e3, e2);
  or or_2 (s0, e3, e1);
endmodule
